// Logisim project control_logic.circ as structural Verilog: 1 circuit, main circuit control_logic
module control_logic (
  input  [31:0] inst,
  input  BrEq,
  input  BrLt,
  output PCSel,
  output RegWEn,
  output [2:0] ImmSel,
  output BrUn,
  output ASel,
  output BSel,
  output [3:0] ALUSel,
  output MemRW,
  output [1:0] WBSel,
  output CSRSel,
  output CSRWen
);

  wire add, add_mul_sub, addi, ALUSel0_I_N, ALUSel0_R, ALUSel1_I_N, ALUSel1_R, ALUSel2_I_N, ALUSel2_R,
       ALUSel3_R, andd, mul, mulh, mulhu, or_2_out, ori, orr, R_Type, sll_mulh, slli, slll, slt, slti, sraa,
       srai, srl_sra, srli, srli_srai, srll, sub, xori, xorr;

  Demultiplexer #(.enable("false"), .select(5)) demultiplexer_1 (
    .out4(BSel), .out7(ImmSel[0]), .out12(R_Type), .in(1'b1), .sel(inst[6:2]));  // open: out0, out1, out2, out3, out5, out6, out8, out9, out10, out11, out13, out14, out15, out16, out17, out18, out19, out20, out21, out22, out23, out24, out25, out26, out27, out28, out29, out30, out31
  Demultiplexer #(.enable("false"), .select(3)) demultiplexer_2 (
    .out0(add_mul_sub), .out1(sll_mulh), .out2(slt), .out3(mulhu), .out4(xorr), .out5(srl_sra), .out6(orr),
    .out7(andd), .in(R_Type), .sel(inst[14:12]));
  Demultiplexer #(.enable("false"), .select(3)) demultiplexer_3 (
    .out0(addi), .out1(slli), .out2(slti), .out4(xori), .out5(srli_srai), .out6(ori), .in(BSel),
    .sel(inst[14:12]));  // open: out3, out7
  or or_1 (RegWEn, R_Type, BSel);
  or or_2 (or_2_out, R_Type, BSel);
  assign WBSel = {{1{1'b0}}, or_2_out};  // Bit_Extender bit_extender_1
  Demultiplexer #(.enable("false"), .select(2)) demultiplexer_4 (
    .out0(add), .out1(mul), .out2(sub), .in(add_mul_sub), .sel({inst[30], inst[25]}));  // open: out3
  or or_3 (ALUSel3_R, mul, sub, mulh, mulhu);
  or or_4 (ALUSel2_R, sub, srll, sraa, slll, slt, mulh);
  or or_5 (ALUSel2_I_N, srli, srai, slli, slti);
  Demultiplexer #(.enable("false")) demultiplexer_5 (.out0(slll), .out1(mulh), .in(sll_mulh), .sel(inst[25]));
  or or_6 (ALUSel1_R, orr, xorr, slll, mulh, slt, mul, mulh);
  or or_7 (ALUSel1_I_N, ori, xori, slli, slti);
  or or_8 (ALUSel0_R, andd, xorr, sraa, slt, mulhu);
  or or_9 (ALUSel0_I_N, slti, srai, xori);
  Demultiplexer #(.enable("false")) demultiplexer_6 (.out0(srll), .out1(sraa), .in(srl_sra), .sel(inst[30]));
  or or_10 (ALUSel[3], ALUSel3_R, 1'b0);
  or or_11 (ALUSel[2], ALUSel2_R, ALUSel2_I_N);
  Demultiplexer #(.enable("false")) demultiplexer_7 (.out0(srli), .out1(srai), .in(srli_srai), .sel(inst[30]));
  or or_12 (ALUSel[1], ALUSel1_R, ALUSel1_I_N);
  or or_13 (ALUSel[0], ALUSel0_R, ALUSel0_I_N);

  assign ASel = 1'b0;
  assign ImmSel[2:1] = 2'b00;
  assign MemRW = 1'b0;
  assign PCSel = 1'b0;
  // also tied to GND on the sheet: ImmSel[0]

  // Other names for the same wires on the sheet: func7low = inst[25]; func7high = inst[30]; I_Type_Normal = BSel;
  //   S_Type = ImmSel[0]

  // Notes on the sheet:
  //   INPUTS to your circuit
  //   DON'T CHANGE THE LOCATIONS OF THE INPUTS AND OUTPUTS!
  //   OUTPUT from your circuit
  //   add/mul/sub
  //   add/mul/sub
  //   and
  //   sll/mulh
  //   or
  //   or
  //   slt
  //   srl/sra
  //   srl/sra
  //   mulhu
  //   xor
  //   xor
endmodule
